// Logisim project Project1.circ as structural Verilog: 1 circuit, main circuit main
module main (
  input  [3:0] Adder,
  input  [3:0] in_2,
  input  [3:0] Set_to_3
);

  wire and_1_out, and_2_out, not_1_out, not_2_out, not_3_out, not_4_out, not_5_out, or_1_out;
  wire [3:0] adder_1_out, divider_1_out, divider_1_rem;

  Adder #(.width(4)) adder_1 (.a(Adder), .b(in_2), .out(adder_1_out));  // open: cin, cout
  Hex_Digit_Display hex_digit_display_1 (.value(adder_1_out));  // open: dp
  Divider #(.width(4)) divider_1 (
    .a(adder_1_out), .b(Set_to_3), .out(divider_1_out), .rem(divider_1_rem));  // open: upper
  LED led_1 (.in(not_1_out));
  not not_1 (not_1_out, adder_1_out[0]);
  or or_1 (or_1_out, divider_1_out[0], divider_1_out[1], divider_1_out[2]);
  LED led_2 (.in(and_2_out));
  not not_2 (not_2_out, divider_1_rem[0]);
  not not_3 (not_3_out, divider_1_rem[1]);
  LED led_3 (.in(and_1_out));
  and and_1 (and_1_out, not_4_out, not_5_out);
  not not_4 (not_4_out, adder_1_out[1]);
  not not_5 (not_5_out, adder_1_out[0]);
  and and_2 (and_2_out, or_1_out, not_2_out, not_3_out);

  // Notes on the sheet:
  //   Bryce Andress
  //   Numbers to be added:
  //   If a number is divisible by 2 the one bit needs to be off
  //   Sum
  //   Divide by 3
  //   Divisible by 2
  //   Get whole number in 1 bit
  //   Make sure there is no remainder
  //   Divisible by 3
  //   Divisible by 4
  //   If a number is divisible by 4 the one and two bit needs t obe off
endmodule
