// Logisim project P3.circ as structural Verilog: 1 circuit, main circuit main
module main (
  input  [1:0] in_1,
  input  [3:0] in_2
);

  wire A, and_1_out, and_2_out, B, BOT, C, CENTER, Clock, D, d_ff_1_q, d_ff_2_q, LL, LR, nand_1_out,
       nand_4_out, nand_5_out, nand_6_out, nand_7_out, nand_9_out, nand_10_out, nand_11_out, nand_13_out,
       nand_14_out, nand_15_out, nand_16_out, not_1_out, not_2_out, not_3_out, not_4_out, not_5_out,
       not_6_out, not_7_out, not_9_out, not_10_out, not_11_out, not_12_out, not_13_out, not_14_out,
       not_15_out, not_16_out, not_17_out, not_18_out, not_19_out, not_20_out, not_21_out, not_22_out,
       not_23_out, not_24_out, not_25_out, not_26_out, not_27_out, not_28_out, not_29_out, TOP, UL, UR;
  wire [3:0] adder_1_out, divider_1_rem, multiplexer_1_out;

  D_Flip_Flop d_ff_1 (.clk(Clock), .D(nand_1_out), .Q(d_ff_1_q));  // open: Qn, preset, en, reset
  nand nand_1 (nand_1_out, 1'b0, d_ff_2_q);
  not not_1 (not_1_out, A);
  not not_2 (not_2_out, B);
  not not_3 (not_3_out, A);
  not not_4 (not_4_out, B);
  not not_5 (not_5_out, C);
  not not_6 (not_6_out, D);
  not not_7 (not_7_out, D);
  Adder #(.width(4)) adder_1 (.a({2'b00, in_1}), .b({A, B, C, D}), .out(adder_1_out));  // open: cin, cout
  Divider #(.width(4)) divider_1 (.a(adder_1_out), .b(4'b1010), .rem(divider_1_rem));  // open: out, upper
  D_Flip_Flop d_ff_2 (.clk(Clock), .D(d_ff_1_q), .Q(d_ff_2_q));  // open: Qn, preset, en, reset
  nand nand_2 (UL, not_1_out, not_2_out);
  nand nand_3 (TOP, not_3_out, not_4_out, not_5_out, not_6_out);
  nand nand_4 (nand_4_out, B, C, not_7_out);
  not not_8 (UR, nand_4_out);
  Multiplexer #(.width(4)) multiplexer_1 (
    .in0(in_2), .in1(divider_1_rem), .out(multiplexer_1_out), .sel(d_ff_2_q));  // open: en
  not not_9 (not_9_out, in_1[1]);
  and and_1 (and_1_out, not_9_out, in_1[0]);
  and and_2 (and_2_out, and_1_out, d_ff_2_q);
  not not_10 (not_10_out, B);
  not not_11 (not_11_out, D);
  not not_12 (not_12_out, and_2_out);
  Counter #(.width(4), .max('h9)) counter_1 (
    .load(not_12_out), .D(multiplexer_1_out), .count(and_2_out), .Q({A, B, C, D}), .clk(Clock));  // open: carry, clr
  Clock clock_1 (.out(Clock));
  not not_13 (not_13_out, A);
  nand nand_5 (nand_5_out, B, C, D);
  not not_14 (not_14_out, B);
  not not_15 (not_15_out, C);
  not not_16 (not_16_out, D);
  nand nand_6 (nand_6_out, not_10_out, C);
  not not_17 (not_17_out, C);
  nand nand_7 (nand_7_out, C, not_11_out);
  Hex_Digit_Display hex_digit_display_1 (.value({A, B, C, D}));  // open: dp
  nand nand_8 (LL, not_13_out, nand_5_out, nand_9_out);
  nand nand_9 (nand_9_out, not_14_out, not_15_out, not_16_out);
  not not_18 (not_18_out, A);
  nand nand_10 (nand_10_out, B, not_17_out, D);
  not not_19 (not_19_out, B);
  nand nand_11 (nand_11_out, not_19_out, not_20_out);
  not not_20 (not_20_out, D);
  nand nand_12 (CENTER, not_18_out, nand_10_out, nand_6_out, nand_7_out, nand_11_out);
  _7_Segment_Display u_7_segment_display_1 (.g(CENTER), .f(UL), .a(TOP), .b(UR), .e(LL), .d(BOT), .c(LR));  // open: dp
  not not_21 (not_21_out, A);
  not not_22 (not_22_out, B);
  not not_23 (not_23_out, C);
  not not_24 (not_24_out, D);
  not not_25 (not_25_out, A);
  not not_26 (not_26_out, B);
  not not_27 (not_27_out, C);
  not not_28 (not_28_out, D);
  not not_29 (not_29_out, B);
  nand nand_13 (nand_13_out, not_21_out, not_22_out, not_23_out, not_24_out);
  nand nand_14 (nand_14_out, not_25_out, not_26_out, not_27_out, not_28_out);
  nand nand_15 (nand_15_out, not_29_out, C, D);
  not not_30 (LR, nand_13_out);
  nand nand_16 (nand_16_out, A, D);
  nand nand_17 (BOT, nand_16_out, nand_14_out, nand_15_out);

  // Notes on the sheet:
  //   UPPER LEFT
  //   TOP
  //   UPPER RIGHT
  //   LOWER LEFT
  //   CENTER
  //   Same B & D as above just for neatness
  //   7 Segment Display
  //   of real number
  //   7 Seg Display of Custom Numbers
  //   LOWER RIGHT
  //   BOTTOM
  //   Same B, C & D as above just for neatness
  //   Project 3
  //   By: Bryce Andress
endmodule
